# Fritzing sketch skin_II_breadboard (saved by Fritzing 0.9.3b)

parts:
  Part1 = LilyPad Arduino Simple Board
  LED1 = smd LED [color="Red (633nm)" package="0603 [SMD]"]
  U1 = POT [package=pot_mammoth]

nets:
  N1: Part1.A3, U1.A
  N2: Part1.D11, LED1.anode
  N3: Part1.GND, LED1.cathode
  N4: Part1.VCC, U1.E
